# Fritzing sketch SingleLED (saved by Fritzing 0.9.2b)
breadboards: 1

parts:
  Part1 = Arduino Uno (Rev3)
  LED1 = LED - 5mm [color="Red (633nm)" package="5 mm [THT]"]
  R1 = Resistor [tolerance=±5% resistance=1k package=THT]
  IR1 = TSOP312.., 314.. [package=THT]

nets:
  N1: Part1.D11_PWM/MOSI, R1.Pin_1
  N2: Part1.GND, LED1.cathode, IR1.Vs
  N3: Part1.D6_PWM, IR1.GND
  N4: Part1.5V, IR1.Data
  N5: LED1.anode, R1.Pin_0
