# Fritzing sketch game (saved by Fritzing 0.9.2b)
breadboards: 1

parts:
  Part1 = Arduino Uno (Rev3)
  IR1 = TSOP312.., 314.. [package=THT]
  LED1 = RGB LED (com. cathode, rgb) [package="5 mm [THT]"]
  LED2 = LED - 5mm [color="Red (633nm)" package="5 mm [THT]"]
  S1 = Pushbutton [package="[THT]"]
  R1 = Resistor [tolerance=±5% resistance=560 package=THT]
  R2 = Resistor [tolerance=±5% resistance=560 package=THT]
  R3 = Resistor [tolerance=±5% resistance=560 package=THT]
  R4 = Resistor [tolerance=±5% resistance=560 package=THT]

nets:
  N1: Part1.D9_PWM, R1.Pin_1
  N2: Part1.D10_PWM/SS, R2.Pin_1
  N3: Part1.D11_PWM/MOSI, R3.Pin_1
  N4: Part1.D12/MISO, R4.Pin_1
  N5: Part1.D13/SCK, S1.Pin_1, S1.Pin_2
  N6: Part1.D6_PWM, IR1.GND
  N7: Part1.5V, IR1.Data, LED1.common_cathode
  N8: Part1.GND, IR1.Vs, LED2.cathode, S1.Pin_3, S1.Pin_4
  N9: LED1.red_anode, R3.Pin_0
  N10: LED1.green_anode, R2.Pin_0
  N11: LED1.blue_anode, R1.Pin_0
  N12: LED2.anode, R4.Pin_0
